// Logisim project fpu_circuito.circ as structural Verilog: 1 circuit, main circuit main
module main (
  input  Sub,
  input  Sinal,
  input  [7:0] Exp,
  input  [22:0] Mantissa,
  input  Sinal_2,
  input  [7:0] Exp_2,
  input  [22:0] Mantissa_2,
  output out_8,
  output [7:0] out_9,
  output [22:0] out_10
);

  wire comparator_1_gt, not_1_out;
  wire [4:0] bit_extender_2_out, bitfinder_1_index, subtractor_3_out;
  wire [7:0] adder_1_out, adder_2_out, bit_extender_1_out, multiplexer_1_out, multiplexer_2_out,
       subtractor_1_out, subtractor_2_out;
  wire [22:0] multiplexer_3_out, multiplexer_6_out;
  wire [23:0] bit_extender_3_out, bit_extender_6_out, multiplexer_8_out, negator_4_out, shifter_2_out;
  wire [24:0] adder_4_out, bit_extender_4_out, bit_extender_5_out, multiplexer_4_out, multiplexer_5_out,
       multiplexer_7_out, negator_1_out, negator_2_out, negator_3_out, shifter_1_out, undriven, undriven_2;

  Adder adder_1 (.a(Exp), .b(8'h7f), .out(adder_1_out));  // open: cin, cout
  Adder adder_2 (.a(Exp_2), .b(8'h7f), .out(adder_2_out));  // open: cin, cout
  Subtractor subtractor_1 (.a(adder_2_out), .b(adder_1_out), .out(subtractor_1_out));  // open: bin, bout
  Subtractor subtractor_2 (.a(adder_1_out), .b(adder_2_out), .out(subtractor_2_out));  // open: bin, bout
  Comparator comparator_1 (.a(adder_1_out), .b(adder_2_out), .gt(comparator_1_gt));  // open: eq, lt
  Multiplexer #(.width(8), .enable("false")) multiplexer_1 (
    .in0(subtractor_1_out), .in1(subtractor_2_out), .out(multiplexer_1_out), .sel(comparator_1_gt));
  Multiplexer #(.width(8), .enable("false")) multiplexer_2 (
    .in0(Exp_2), .in1(Exp), .out(multiplexer_2_out), .sel(comparator_1_gt));
  assign bit_extender_1_out = {{3{1'b0}}, subtractor_3_out};  // Bit_Extender bit_extender_1
  not not_1 (not_1_out, comparator_1_gt);
  Multiplexer #(.width(23), .enable("false")) multiplexer_3 (
    .in0(Mantissa), .in1(Mantissa_2), .out(multiplexer_3_out), .sel(not_1_out));
  Bit_Extender #(.out_width(5)) bit_extender_2 (.in(multiplexer_1_out), .out(bit_extender_2_out));
  Negator #(.width(25)) negator_1 (.in(undriven), .out(negator_1_out));
  Multiplexer #(.width(25), .enable("false")) multiplexer_4 (
    .in0(undriven), .in1(negator_1_out), .out(multiplexer_4_out), .sel(Sinal));
  Adder adder_3 (.a(multiplexer_2_out), .b(bit_extender_1_out), .out(out_9));  // open: cin, cout
  assign bit_extender_3_out = {{1{1'b1}}, multiplexer_3_out};  // Bit_Extender bit_extender_3
  Negator #(.width(25)) negator_2 (.in(undriven_2), .out(negator_2_out));
  assign bit_extender_4_out = {{1{1'b0}}, bit_extender_3_out};  // Bit_Extender bit_extender_4
  Multiplexer #(.width(25), .enable("false")) multiplexer_5 (
    .in0(undriven_2), .in1(negator_2_out), .out(multiplexer_5_out), .sel(Sinal_2));
  Adder #(.width(25)) adder_4 (
    .a(bit_extender_5_out), .b(bit_extender_4_out), .out(adder_4_out), .cout(out_8));  // open: cin
  Multiplexer #(.width(23), .enable("false")) multiplexer_6 (
    .in0(Mantissa), .in1(Mantissa_2), .out(multiplexer_6_out), .sel(comparator_1_gt));
  assign bit_extender_5_out = {{1{1'b0}}, multiplexer_8_out};  // Bit_Extender bit_extender_5
  Negator #(.width(25)) negator_3 (.in(adder_4_out), .out(negator_3_out));
  Multiplexer #(.width(25), .enable("false")) multiplexer_7 (
    .in0(adder_4_out), .in1(negator_3_out), .out(multiplexer_7_out), .sel(out_8));
  BitFinder #(.width(25), .\type ("high1")) bitfinder_1 (
    .in(multiplexer_7_out), .index(bitfinder_1_index));  // open: found
  assign bit_extender_6_out = {{1{1'b1}}, multiplexer_6_out};  // Bit_Extender bit_extender_6
  Subtractor #(.width(5)) subtractor_3 (
    .a(bitfinder_1_index), .b(5'b10111), .out(subtractor_3_out));  // open: bin, bout
  Shifter #(.width(25), .shift("lr")) shifter_1 (
    .in(multiplexer_7_out), .\dist (subtractor_3_out), .out(shifter_1_out));
  Shifter #(.width(24), .shift("lr")) shifter_2 (
    .in(bit_extender_6_out), .\dist (bit_extender_2_out), .out(shifter_2_out));
  Bit_Extender #(.in_width(25), .out_width(23)) bit_extender_7 (.in(shifter_1_out), .out(out_10));
  Negator #(.width(24)) negator_4 (.in(shifter_2_out), .out(negator_4_out));
  Multiplexer #(.width(24), .enable("false")) multiplexer_8 (
    .in0(shifter_2_out), .in1(negator_4_out), .out(multiplexer_8_out), .sel(Sub));

  // Other names for the same wires on the sheet: exp_A[7:0] = Exp; exp_B[7:0] = Exp_2; sinal_A = Sinal;
  //   sinal_B = Sinal_2

  // Notes on the sheet:
  //   A
  //   B-A
  //   A-B
  //   Unidade de ponto flutuante FPU
  //   LOD
  //   B
  //   Complemento de dois
  //   Normalização do número
endmodule
